// Logisim project DLD_Project_1.0.circ as structural Verilog: 1 circuit, main circuit main
module main (
  input  A,
  input  B,
  input  C,
  input  D,
  output V,
  output W,
  output X,
  output Y,
  output Z
);

  wire AND1_out, AND2_out, AND3_out, AND4_out, AND5_out, AND6_out, AND7_out, INV1_out, INV2_out, INV3_out,
       OR1_out, XOR1_out;

  and AND1 (AND1_out, B, C);
  and AND2 (AND2_out, B, D);
  or OR1 (OR1_out, AND1_out, AND2_out);
  not INV1 (INV1_out, D);
  or OR2 (Z, A, OR1_out);
  and AND3 (AND3_out, A, INV1_out);
  or OR3 (Y, B, AND3_out);
  and AND4 (AND4_out, D, C);
  or OR4 (X, B, AND4_out);
  not INV3 (INV3_out, A);
  not INV2 (INV2_out, C);
  xor XOR1 (XOR1_out, B, C);
  and AND5 (AND5_out, C, INV1_out);
  or OR5 (W, XOR1_out, AND5_out);
  and AND6 (AND6_out, INV3_out, INV2_out);
  and AND7 (AND7_out, AND6_out, D);
  or OR6 (V, AND7_out, XOR1_out);

  // Notes on the sheet:
  //   AND = 2 NAND
  //   OR = 3 NAND
  //   XOR = !AB+A!B = (A+B)(!A+!B) = (A+B)!(AB)
  //   XOR1 can be replaced with !(AB)(A+B) uwing two and gates, an or gate, and an inverter, or one nand gate, one or gate, and one and gate
endmodule
