// Logisim project DLD_Project_1.circ as structural Verilog: 1 circuit, main circuit main
module main (
  input  A,
  input  B,
  input  C,
  input  D,
  output V,
  output W,
  output X,
  output Y,
  output Z
);

  wire AND1_out, AND2_out, AND3_out, AND4_out, AND5_out, AND6_out, AND7_out, AND8_out, INV1_out, INV2_2_out,
       INV2_out, INV3_out, INV4_out, INV5_out, OR1_out, OR7_out, OR8_out;

  and AND1 (AND1_out, B, C);
  and AND2 (AND2_out, B, D);
  or OR1 (OR1_out, AND1_out, AND2_out);
  not INV1 (INV1_out, D);
  or OR2 (Z, A, OR1_out);
  and AND3 (AND3_out, A, INV1_out);
  or OR3 (Y, B, AND3_out);
  and AND4 (AND4_out, D, C);
  not INV2_2 (INV2_2_out, C);
  or OR7 (OR7_out, INV2_2_out, B);
  or OR8 (OR8_out, C, INV4_out);
  not INV4 (INV4_out, B);
  or OR4 (X, B, AND4_out);
  and AND8 (AND8_out, OR7_out, OR8_out);
  not INV3 (INV3_out, A);
  not INV2 (INV2_out, C);
  not INV5 (INV5_out, AND8_out);
  // NoConnect on INV5_out
  // XOR_Gate XOR1 has open pins: in0=B, in1=C, out=open
  and AND5 (AND5_out, C, INV1_out);
  or OR5 (W, INV5_out, AND5_out);
  and AND6 (AND6_out, INV3_out, INV2_out);
  and AND7 (AND7_out, AND6_out, D);
  or OR6 (V, AND7_out, INV5_out);

  // Notes on the sheet:
  //   5 Gate Solution
  //   INV2_2, INV4, OR7, OR8, AND8, and INV5 Eliminate XOR1
  //   2 Quad Input And Chips, 2 Quad Input Or Chips, and 1 Hex Inverter Chip
endmodule
