// Logisim project not.circ as structural Verilog: 1 circuit, main circuit main
module main (
  input  NAND_IN,
  input  NOR_IN,
  output NAND_OUT,
  output NOR_OUT
);

  nand nand_1 (NAND_OUT, NAND_IN, NAND_IN);
  nor nor_1 (NOR_OUT, NOR_IN, NOR_IN);
endmodule
