// Logisim project ddr.circ as structural Verilog: 1 circuit, main circuit main
module main (
);

  wire and_1_out, button_1_out, clock_1_out, d_ff_1_q, d_ff_2_q, n74164_1_pin1, n74164_1_pin2, n74164_1_pin3,
       n74164_1_pin4, n74164_1_pin5, n74164_1_pin6, n74164_1_pin9, n74164_1_pin10, n74164_1_pin11,
       n74164_1_pin12, n74164_1_pin13, not_1_out, random_1_out, random_2_out, random_3_out, random_4_out,
       xor_1_out, xor_2_out, xor_4_out;

  Clock clock_1 (.out(clock_1_out));
  Random #(.seed(356346534), .width(1)) random_1 (.clr(not_1_out), .next(1'b1), .clk(clock_1_out), .out(random_1_out));
  not not_1 (not_1_out, 1'b1);
  Random #(.seed(42384523), .width(1)) random_2 (.clr(not_1_out), .clk(clock_1_out), .out(random_2_out));  // open: next
  Random #(.seed(2), .width(1)) random_3 (.clr(not_1_out), .clk(clock_1_out), .out(random_3_out));  // open: next
  Random #(.seed(234423), .width(1)) random_4 (.clr(not_1_out), .clk(clock_1_out), .out(random_4_out));  // open: next
  _74164 u_74164_1 (
    .pin1(n74164_1_pin1), .pin2(n74164_1_pin2), .pin3(n74164_1_pin3), .pin4(n74164_1_pin4),
    .pin5(n74164_1_pin5), .pin6(n74164_1_pin6), .pin13(n74164_1_pin13), .pin12(n74164_1_pin12),
    .pin11(n74164_1_pin11), .pin10(n74164_1_pin10), .pin9(n74164_1_pin9), .pin8(clock_1_out));
  LED led_1 (.in(n74164_1_pin3));
  LED led_2 (.in(n74164_1_pin4));
  xor xor_1 (xor_1_out, random_1_out, random_2_out);
  xor xor_2 (xor_2_out, random_3_out, random_4_out);
  LED led_3 (.in(n74164_1_pin5));
  LED led_4 (.in(n74164_1_pin6));
  LED led_5 (.in(n74164_1_pin10));
  LED led_6 (.in(n74164_1_pin11));
  xor xor_3 (n74164_1_pin1, xor_1_out, xor_2_out);
  LED led_7 (.in(n74164_1_pin12));
  LED led_8 (.in(n74164_1_pin13));
  Button button_1 (.out(button_1_out));
  D_Flip_Flop #(.trigger("falling")) d_ff_1 (
    .D(n74164_1_pin13), .clk(clock_1_out), .Q(d_ff_1_q));  // open: Qn, preset, reset
  D_Flip_Flop #(.trigger("falling")) d_ff_2 (
    .D(button_1_out), .clk(clock_1_out), .Q(d_ff_2_q));  // open: Qn, preset, reset
  and and_1 (and_1_out, d_ff_1_q, d_ff_2_q);
  xor xor_4 (xor_4_out, d_ff_1_q, d_ff_2_q);
  // also tied to VCC on the sheet: {n74164_1_pin2, n74164_1_pin9}
endmodule
