// Logisim project hw1DLD.circ as structural Verilog: 1 circuit, main circuit main
module main (
  input  A,
  input  B,
  output W,
  output X,
  output Y,
  output D
);

  wire not_1_out;

  not not_1 (not_1_out, A);
  and and_1 (D, A, B);
  or or_1 (X, A, B);
  or or_2 (W, A, not_1_out);

  assign Y = A;
endmodule
